// Logisim project EXP-38 LOGICAL OPERATION LOGISIM.circ as structural Verilog: 1 circuit, main circuit main
module main (
  input  in_1,
  input  in_2,
  input  in_3,
  input  in_4,
  input  in_5,
  output out_6,
  output out_7,
  output out_8
);

  and and_1 (out_6, in_1, in_2);
  or or_1 (out_7, in_3, in_4);
  not not_1 (out_8, in_5);
endmodule
